# Fritzing sketch louie (saved by Fritzing 0.8.5b)
circuit board: 8.46667cm x 5.64444cm
breadboards: 1

parts:
  Q1 = Basic FET P-Channel [package="TO220 [THT]"]
  VCC1 = Battery
  U1 = attiny85 [package=dip]
  D1 = Rectifier Diode [part_number=1N4001 package="300 mil [THT]"]
  J1 = Power Jack [package=power_jack_pth]
  10kΩ = Resistor [tolerance=±5% resistance=10k package=THT]
  10kΩ_2 = Resistor [tolerance=±5% resistance=10k package=THT]
  S4 = Toggle Switch [package=THT]
  C1 = Electrolytic Capacitor [capacitance=1µF package="100 mil [THT, electrolytic]"]

nets:
  N1: Q1.gate, U1.Pin_5
  N2: Q1.drain, D1.anode, J1.PWR
  N3: Q1.source, VCC1.-, U1.Pin_4, 10kΩ.Pin_0, 10kΩ_2.Pin_0, C1.-
  N4: VCC1.+, U1.Pin_8, D1.cathode, J1.GND, S4.COM, C1.+
  N5: U1.Pin_2, 10kΩ.Pin_1, S4.L1
  N6: U1.Pin_3, 10kΩ_2.Pin_1, S4.L2
